// Digital circuit BCD-Taschenrechner.dig as structural Verilog
module BCD_Taschenrechner (
);

  wire _0, _1, _2, _3, _4, _5, _6, _7, _8, _9, eq, plus, tunnel, tunnel_t, tunnel_t_t;
  wire [3:0] \input ;

  Button button_1 (.out(_1));
  Button button_2 (.out(_5));
  Button button_3 (.out(_9));
  Button button_4 (.out(tunnel));
  Button button_5 (.out(_2));
  Button button_6 (.out(_6));
  Button button_7 (.out(_0));
  Button button_8 (.out(tunnel_t_t));
  Button button_9 (.out(_3));
  Button button_10 (.out(_7));
  Button button_11 (.out(plus));
  Button button_12 (.out(_4));
  Button button_13 (.out(_8));
  Button button_14 (.out(tunnel_t));
  Button button_15 (.out(eq));
  or or_1 (\input [0], _1, _3, _5, _7, _9);
  or or_2 (\input [1], _2, _3, _6, _7);
  or or_3 (\input [2], _4, _5, _6, _7);
  or or_4 (\input [3], _8, _9);
  Seven_Seg_Hex seven_seg_hex_1 (.d(\input ), .dp(1'b0));
  Seven_Seg_Hex seven_seg_hex_2 (.d(\input ), .dp(1'b0));
  Seven_Seg_Hex seven_seg_hex_3 (.d(\input ), .dp(1'b0));
  Seven_Seg_Hex seven_seg_hex_4 (.d(\input ), .dp(1'b0));
  Seven_Seg_Hex seven_seg_hex_5 (.d(\input ), .dp(1'b0));

  // Notes on the sheet:
  //   Logic for encoding button input to BCD number.
  //   B0 = T1 + T3 + T5 + T7 + T9
  //   B1 = T2 + T3 + T6 + T7
  //   B2 = T4 + T5 + T6 + T7
  //   B3 = T8 + T9
endmodule
